# Fritzing sketch iot-project (saved by Fritzing 0.9.3b)
circuit board: 6.88356cm x 7.96248cm

parts:
  Part1 = RFID-RC522-v2
  LED1 = LED - 3mm [color="Red (633nm)" package="3 mm [THT]"]
  LED2 = LED - 3mm [color="Green (555nm)" package="3 mm [THT]"]
  SERVO1 = Tower Pro SG90 servo [part_number=101246]
  R1 = Resistor [tolerance=±5% resistance=220 package="0603 [SMD]"]
  J1 = Piezo Speaker
  MH-ET_LIVE_ESP32_DEVKIT1 = MH-ET LIVE ESP32 DEVKIT 38 pins

nets:
  N1: Part1.SDA, MH-ET_LIVE_ESP32_DEVKIT1.IO5
  N2: Part1.SCK, MH-ET_LIVE_ESP32_DEVKIT1.IO18
  N3: Part1.MOSI, MH-ET_LIVE_ESP32_DEVKIT1.IO23
  N4: Part1.MISO, MH-ET_LIVE_ESP32_DEVKIT1.IO19
  3.3V: Part1.3.3V, MH-ET_LIVE_ESP32_DEVKIT1.3V3
  N5: LED1.cathode, LED2.cathode, R1.Pin_0, R1.Pin_1, J1.pin1, MH-ET_LIVE_ESP32_DEVKIT1.GND#58
  N6: LED1.anode, MH-ET_LIVE_ESP32_DEVKIT1.IO34, MH-ET_LIVE_ESP32_DEVKIT1.IO35
  N7: LED2.anode, MH-ET_LIVE_ESP32_DEVKIT1.IO25
  N8: SERVO1.Signal, MH-ET_LIVE_ESP32_DEVKIT1.IO33
  +5V: SERVO1.+5V, MH-ET_LIVE_ESP32_DEVKIT1.5V
  N9: SERVO1.GND, MH-ET_LIVE_ESP32_DEVKIT1.GND#64
  N10: J1.pin2, MH-ET_LIVE_ESP32_DEVKIT1.IO27

custom parts:
  RFID-RC522-v2: A simple China made RFID-RC522 Reader; do check the pin labels, as this is a MFRC522 based clone.
  Tower Pro SG90 servo: Original file by John De Cristofaro http://www.adafruit.com/products/1449 Adafruit Feedback Servo (Small) Edited by: e-radionica.com 28/9/2015
  MH-ET LIVE ESP32 DEVKIT 38 pins: http://mh.nodebb.com/topic/2/mh-et-live-esp32-devkit
