# Fritzing sketch mfrc522.py (saved by Fritzing 0.9.3b)
breadboards: 1

parts:
  MH-ET_LIVE_ESP32_DEVKIT1 = MH-ET LIVE ESP32 DEVKIT 38 pins
  Part1 = RFID-RC522-v2

nets:
  3V3: MH-ET_LIVE_ESP32_DEVKIT1.3V3, Part1.3.3V

custom parts:
  MH-ET LIVE ESP32 DEVKIT 38 pins: http://mh.nodebb.com/topic/2/mh-et-live-esp32-devkit
  RFID-RC522-v2: A simple China made RFID-RC522 Reader; do check the pin labels, as this is a MFRC522 based clone.
